// Logisim project Projeto1.circ as structural Verilog: 6 circuits, main circuit Caixa_Sensores
module main (
);

  wire caixa_displaycaixa1_1_a, caixa_displaycaixa1_1_b, caixa_displaycaixa1_1_c, caixa_displaycaixa1_1_d,
       caixa_displaycaixa1_1_e, caixa_displaycaixa1_1_f, caixa_displaycaixa1_1_g, caixa_displaycaixa2_1_a,
       caixa_displaycaixa2_1_b, caixa_displaycaixa2_1_c, caixa_displaycaixa2_1_d, caixa_displaycaixa2_1_e,
       caixa_displaycaixa2_1_f, caixa_displaycaixa2_1_g, caixa_sensores_1_bomba,
       caixa_sensores_1_eletrovalvula, xswitch_1_p1, xswitch_2_p1, xswitch_3_p1;
  wire [6:0] caixa_matrizcaixa1_1_out_4, caixa_matrizcaixa1_1_out_5, caixa_matrizcaixa2_1_out_4,
       caixa_matrizcaixa2_1_out_5;

  // XSwitch xswitch_1: pin names not known; wires that end beside it: xswitch_1_p1
  // XSwitch xswitch_2: pin names not known; wires that end beside it: xswitch_2_p1
  // XSwitch xswitch_3: pin names not known; wires that end beside it: xswitch_3_p1
  Caixa_DisplayCaixa1 caixa_displaycaixa1_1 (
    .SensorA(xswitch_2_p1), .SensorB(xswitch_1_p1), .SensorC(xswitch_3_p1), .a(caixa_displaycaixa1_1_a),
    .b(caixa_displaycaixa1_1_b), .c(caixa_displaycaixa1_1_c), .d(caixa_displaycaixa1_1_d),
    .e(caixa_displaycaixa1_1_e), .f(caixa_displaycaixa1_1_f), .g(caixa_displaycaixa1_1_g));
  Caixa_DisplayCaixa2 caixa_displaycaixa2_1 (
    .SensorA(xswitch_2_p1), .SensorB(xswitch_1_p1), .SensorC(xswitch_3_p1), .a(caixa_displaycaixa2_1_a),
    .b(caixa_displaycaixa2_1_b), .c(caixa_displaycaixa2_1_c), .d(caixa_displaycaixa2_1_d),
    .e(caixa_displaycaixa2_1_e), .f(caixa_displaycaixa2_1_f), .g(caixa_displaycaixa2_1_g));
  Caixa_MatrizCaixa1 caixa_matrizcaixa1_1 (
    .SensorA(xswitch_2_p1), .SensorB(xswitch_1_p1), .SensorC(xswitch_3_p1),
    .out_4(caixa_matrizcaixa1_1_out_4), .out_5(caixa_matrizcaixa1_1_out_5));
  Caixa_MatrizCaixa2 caixa_matrizcaixa2_1 (
    .SensorA(xswitch_2_p1), .SensorB(xswitch_1_p1), .SensorC(xswitch_3_p1),
    .out_4(caixa_matrizcaixa2_1_out_4), .out_5(caixa_matrizcaixa2_1_out_5));
  Caixa_Sensores caixa_sensores_1 (
    .SensorA(xswitch_2_p1), .SensorB(xswitch_1_p1), .SensorC(xswitch_3_p1), .Bomba(caixa_sensores_1_bomba),
    .EletroValvula(caixa_sensores_1_eletrovalvula));
  LED Bomba (.in(caixa_sensores_1_bomba));
  LED Eletro_Valvula (.in(caixa_sensores_1_eletrovalvula));
  _7_Segment_Display u_7_segment_display_1 (
    .g(caixa_displaycaixa1_1_g), .f(caixa_displaycaixa1_1_f), .a(caixa_displaycaixa1_1_a),
    .b(caixa_displaycaixa1_1_b), .e(caixa_displaycaixa1_1_e), .d(caixa_displaycaixa1_1_d),
    .c(caixa_displaycaixa1_1_c));  // open: dp
  _7_Segment_Display u_7_segment_display_2 (
    .g(caixa_displaycaixa2_1_g), .f(caixa_displaycaixa2_1_f), .a(caixa_displaycaixa2_1_a),
    .b(caixa_displaycaixa2_1_b), .e(caixa_displaycaixa2_1_e), .d(caixa_displaycaixa2_1_d),
    .c(caixa_displaycaixa2_1_c));  // open: dp
  DotMatrix dotmatrix_1 (
    .col0(caixa_matrizcaixa1_1_out_4), .col1(caixa_matrizcaixa1_1_out_5), .col3(caixa_matrizcaixa2_1_out_4),
    .col4(caixa_matrizcaixa2_1_out_5));  // open: col2

  // Notes on the sheet:
  //   B
  //   A
  //   C
  //   ---Não detectou
  //   ---Detectou
  //   CAIXA 1
  //   CAIXA 2
  //   C1    C2
  //   --------------Full
  //   --------------Half
  //   --------------Empty
  //   LEGENDA:
  //   Caixa 1:
  //   H - half
  //   F - full
  //   LEDs:
  //   Sensores:
  //   E - empty
  //   Ev Acesa - Ev em funcionamento
  //   A - Sensor Superior da Caixa1
  //   B - Sensor Inferior da Caixa1
  //   C - Sensor Unico da Caixa2
  //   Caixa 2:
  //   E - empty
  //   F - full
  //   Bomba Acesa - bomba em funcionamento
endmodule

module Caixa_Sensores (
  input  SensorA,
  input  SensorB,
  input  SensorC,
  output Bomba,
  output EletroValvula
);

  wire not_1_out;

  not not_1 (not_1_out, SensorC);
  not not_2 (EletroValvula, SensorA);
  and and_1 (Bomba, SensorB, not_1_out);
endmodule

module Caixa_DisplayCaixa1 (
  input  SensorA,
  input  SensorB,
  input  SensorC,
  output a,
  output b,
  output c,
  output d,
  output e,
  output f,
  output g
);

  wire and_1_out, and_2_out, not_1_out, not_2_out, not_3_out, not_4_out, not_5_out, not_6_out, not_7_out,
       not_8_out, not_9_out;

  not not_1 (not_1_out, SensorA);
  not not_2 (not_2_out, SensorB);
  not not_3 (not_3_out, SensorA);
  not not_4 (not_4_out, SensorA);
  not not_5 (not_5_out, SensorA);
  not not_6 (not_6_out, SensorB);
  not not_7 (not_7_out, SensorA);
  not not_8 (not_8_out, SensorA);
  not not_9 (not_9_out, SensorA);
  and and_1 (and_1_out, not_1_out, not_2_out);
  and and_2 (and_2_out, SensorA, SensorB);
  and and_3 (b, not_3_out, SensorB);
  and and_4 (c, not_4_out, SensorB);
  and and_5 (d, not_5_out, not_6_out);
  or or_1 (e, not_7_out, SensorB);
  or or_2 (f, not_8_out, SensorB);
  or or_3 (g, not_9_out, SensorB);
  or or_4 (a, and_1_out, and_2_out);
endmodule

module Caixa_DisplayCaixa2 (
  input  SensorA,
  input  SensorB,
  input  SensorC,
  output a,
  output b,
  output c,
  output d,
  output e,
  output f,
  output g
);

  wire and_1_out, and_2_out, not_1_out, not_2_out, not_3_out, not_4_out, not_5_out, not_6_out, not_7_out;

  not not_1 (not_1_out, SensorA);
  not not_2 (not_2_out, SensorA);
  not not_3 (not_3_out, SensorC);
  not not_4 (not_4_out, SensorC);
  not not_5 (not_5_out, SensorA);
  not not_6 (not_6_out, SensorA);
  not not_7 (not_7_out, SensorA);
  or or_1 (a, not_1_out, SensorB);
  and and_1 (and_1_out, not_2_out, not_3_out);
  and and_2 (and_2_out, SensorB, not_4_out);
  or or_2 (e, not_5_out, SensorB);
  or or_3 (f, not_6_out, SensorB);
  or or_4 (g, not_7_out, SensorB);
  or or_5 (d, and_1_out, and_2_out);

  assign b = 1'b0;
  assign c = 1'b0;
endmodule

module Caixa_MatrizCaixa2 (
  input  SensorA,
  input  SensorB,
  input  SensorC,
  output [6:0] out_4,
  output [6:0] out_5
);

  wire and_1_out, and_2_out, and_3_out, and_4_out, and_5_out, and_6_out, and_7_out, and_8_out, and_9_out,
       and_10_out, and_11_out, and_12_out, not_1_out, not_2_out, not_3_out, not_4_out, not_5_out, not_6_out,
       not_7_out;

  not not_1 (not_1_out, SensorA);
  not not_2 (not_2_out, SensorA);
  not not_3 (not_3_out, SensorA);
  not not_4 (not_4_out, SensorA);
  not not_5 (not_5_out, SensorA);
  not not_6 (not_6_out, SensorA);
  not not_7 (not_7_out, SensorA);
  or or_1 (out_4[0], not_1_out, SensorB);
  and and_1 (and_1_out, not_2_out, SensorC);
  and and_2 (and_2_out, SensorB, SensorC);
  and and_3 (and_3_out, not_3_out, SensorC);
  and and_4 (and_4_out, SensorB, SensorC);
  and and_5 (and_5_out, not_4_out, SensorC);
  and and_6 (and_6_out, SensorB, SensorC);
  and and_7 (and_7_out, not_5_out, SensorC);
  and and_8 (and_8_out, SensorB, SensorC);
  and and_9 (and_9_out, not_6_out, SensorC);
  and and_10 (and_10_out, SensorB, SensorC);
  and and_11 (and_11_out, not_7_out, SensorC);
  and and_12 (and_12_out, SensorB, SensorC);
  or or_2 (out_4[1], and_1_out, and_2_out);
  or or_3 (out_4[2], and_3_out, and_4_out);
  or or_4 (out_4[3], and_5_out, and_6_out);
  or or_5 (out_4[4], and_7_out, and_8_out);
  or or_6 (out_4[5], and_9_out, and_10_out);
  or or_7 (out_4[6], and_11_out, and_12_out);

  assign out_5 = out_4;
endmodule

module Caixa_MatrizCaixa1 (
  input  SensorA,
  input  SensorB,
  input  SensorC,
  output [6:0] out_4,
  output [6:0] out_5
);

  wire not_1_out;

  not not_1 (not_1_out, SensorA);
  and and_1 (out_4[4], SensorA, SensorB);
  and and_2 (out_4[5], SensorA, SensorB);
  and and_3 (out_4[6], SensorA, SensorB);
  or or_1 (out_4[0], not_1_out, SensorB);

  assign out_4[3:1] = {3{SensorB}};
  assign out_5 = {out_4[6:4], {3{SensorB}}, out_4[0]};
endmodule
