// Logisim project Projeto2.circ as structural Verilog: 3 circuits, main circuit main
module main (
);

  wire A_p1, B_p1, C_p1, caixa_alarme_1_out_5, caixa_alarme_1_out_6, K_p1;

  // XSwitch B: pin names not known; wires that end beside it: B_p1
  // XSwitch A: pin names not known; wires that end beside it: A_p1
  // XSwitch K: pin names not known; wires that end beside it: K_p1
  // XSwitch C: pin names not known; wires that end beside it: C_p1
  Caixa_Alarme caixa_alarme_1 (
    .SensorA(A_p1), .SensorB(B_p1), .SensorC(C_p1), .ChaveK(K_p1), .out_5(caixa_alarme_1_out_5),
    .out_6(caixa_alarme_1_out_6));
  LED Porta_Direita (.in(A_p1));
  LED Porta_Esquerda (.in(B_p1));
  LED \Presença  (.in(C_p1));
  LED Alarme (.in(caixa_alarme_1_out_5));
  // Buzzer buzzer_1: pin names not known; wires that end beside it: caixa_alarme_1_out_6

  // Notes on the sheet:
  //   ---Não detectou / Desativada
  //   ---Detectou / Ativada
  //   LEGENDA:
  //   Entradas:
  //   LEDs:
  //   A - Sensor da porta direita
  //   B - Sensor da porta esquerda
  //   C - Sensor de presença
  //   K - Chave do alarme
  //   Porta Direita acesa - porta aberta
  //   Porta Esquerda acesa - porta aberta
  //   Presença acesa - presença no carro detectada
  //   Alarme aceso - alarme disparado
endmodule

module Caixa_Alarme (
  input  SensorA,
  input  SensorB,
  input  SensorC,
  input  ChaveK,
  output out_5,
  output out_6
);

  wire and_1_out, and_2_out, or_1_out;

  and and_1 (and_1_out, SensorB, SensorC, ChaveK);
  and and_2 (and_2_out, SensorA, SensorC, ChaveK);
  Caixa_LedPiscante caixa_ledpiscante_1 (.AlarmeIn(or_1_out), .AlarmeOut(out_5));
  or or_1 (or_1_out, and_1_out, and_2_out);

  assign out_6 = out_5;
endmodule

module Caixa_LedPiscante (
  input  AlarmeIn,
  output AlarmeOut
);

  wire clock_1_out;

  Clock clock_1 (.out(clock_1_out));
  and and_1 (AlarmeOut, AlarmeIn, clock_1_out);
endmodule
