// Logisim project projeto4.circ as structural Verilog: 4 circuits, main circuit main
module main (
);

  wire caixa_display1_1_a, caixa_display1_1_b, caixa_display1_1_c, caixa_display1_1_d, caixa_display1_1_e,
       caixa_display1_1_f, caixa_display1_1_g, caixa_display2_1_a, caixa_display2_1_b, caixa_display2_1_c,
       caixa_display2_1_d, caixa_display2_1_e, caixa_display2_1_f, caixa_display2_1_g, caixa_telefones_1_sas,
       caixa_telefones_1_sre, caixa_telefones_1_sse, caixa_telefones_1_svr, xswitch_1_p1, xswitch_2_p1,
       xswitch_3_p1, xswitch_4_p1;

  // XSwitch xswitch_1: pin names not known; wires that end beside it: xswitch_1_p1
  // XSwitch xswitch_2: pin names not known; wires that end beside it: xswitch_2_p1
  // XSwitch xswitch_3: pin names not known; wires that end beside it: xswitch_3_p1
  // XSwitch xswitch_4: pin names not known; wires that end beside it: xswitch_4_p1
  Caixa_Telefones caixa_telefones_1 (
    .RE(xswitch_2_p1), .VR(xswitch_1_p1), .AS(xswitch_3_p1), .SE(xswitch_4_p1), .SRE(caixa_telefones_1_sre),
    .SVR(caixa_telefones_1_svr), .SAS(caixa_telefones_1_sas), .SSE(caixa_telefones_1_sse));
  Caixa_Display1 caixa_display1_1 (
    .RE(xswitch_2_p1), .VR(xswitch_1_p1), .AS(xswitch_3_p1), .SE(xswitch_4_p1), .a(caixa_display1_1_a),
    .b(caixa_display1_1_b), .c(caixa_display1_1_c), .d(caixa_display1_1_d), .e(caixa_display1_1_e),
    .f(caixa_display1_1_f), .g(caixa_display1_1_g));
  Caixa_Display2 caixa_display2_1 (
    .RE(xswitch_2_p1), .VR(xswitch_1_p1), .AS(xswitch_3_p1), .SE(xswitch_4_p1), .a(caixa_display2_1_a),
    .b(caixa_display2_1_b), .c(caixa_display2_1_c), .d(caixa_display2_1_d), .e(caixa_display2_1_e),
    .f(caixa_display2_1_f), .g(caixa_display2_1_g));
  LED RE (.in(caixa_telefones_1_sre));
  _7_Segment_Display u_7_segment_display_1 (
    .g(caixa_display1_1_g), .f(caixa_display1_1_f), .a(caixa_display1_1_a), .b(caixa_display1_1_b),
    .e(caixa_display1_1_e), .d(caixa_display1_1_d), .c(caixa_display1_1_c));  // open: dp
  LED AS (.in(caixa_telefones_1_sas));
  LED VR (.in(caixa_telefones_1_svr));
  _7_Segment_Display u_7_segment_display_2 (
    .g(caixa_display2_1_g), .f(caixa_display2_1_f), .a(caixa_display2_1_a), .b(caixa_display2_1_b),
    .e(caixa_display2_1_e), .d(caixa_display2_1_d), .c(caixa_display2_1_c));  // open: dp
  LED SE (.in(caixa_telefones_1_sse));

  // Notes on the sheet:
  //   TVR
  //   TRE
  //   TSE
  //   TAR
  //   ---Chamada não recebida
  //   ---Chamada recebida
  //   LEGENDA:
  //   Telefones:
  //   LEDs e Display:
  //   TRE - Chamada recebida pelo reitor
  //   TVR - Chamada recebida pelo vice-reitor
  //   TAR - Chamada recebida pelo assessor
  //   TSE - Chamada recebida pela secretária
  //   RE Aceso - Chamada atendida pelo reitor
  //   VR Aceso - Chamada atendida pelo vice-reitor
  //   AR Aceso - Chamada atendida pelo assessor
  //   SE Aceso - Chamada atendida pela secretária
endmodule

module Caixa_Telefones (
  input  RE,
  input  VR,
  input  AS,
  input  SE,
  output SRE,
  output SVR,
  output SAS,
  output SSE
);

  wire not_1_out, not_2_out, not_3_out, not_4_out, not_5_out, not_6_out;

  not not_1 (not_1_out, RE);
  and and_1 (SVR, not_1_out, VR);
  not not_2 (not_2_out, RE);
  not not_3 (not_3_out, VR);
  and and_2 (SAS, not_2_out, not_3_out, AS);
  not not_4 (not_4_out, RE);
  not not_5 (not_5_out, VR);
  not not_6 (not_6_out, AS);
  and and_3 (SSE, not_4_out, not_5_out, not_6_out, SE);
  // Beeper beeper_1: pin names not known; wires that end beside it: RE
  // Beeper beeper_2: pin names not known; wires that end beside it: SVR
  // Beeper beeper_3: pin names not known; wires that end beside it: SAS
  // Beeper beeper_4: pin names not known; wires that end beside it: SSE

  assign SRE = RE;
endmodule

module Caixa_Display1 (
  input  RE,
  input  VR,
  input  AS,
  input  SE,
  output a,
  output b,
  output c,
  output d,
  output e,
  output f,
  output g
);

  wire and_1_out, and_2_out, and_3_out, and_4_out, and_5_out, and_6_out, and_7_out, and_8_out, and_9_out,
       and_10_out, not_1_out, not_2_out, not_3_out, not_4_out, not_5_out, not_6_out, not_7_out, not_8_out,
       not_9_out, not_10_out, not_11_out, not_12_out, not_13_out;

  not not_1 (not_1_out, VR);
  and and_1 (and_1_out, not_1_out, SE);
  not not_2 (not_2_out, VR);
  and and_2 (and_2_out, not_2_out, AS);
  or or_1 (b, AS, VR, RE);
  not not_3 (not_3_out, RE);
  and and_3 (and_3_out, not_3_out, SE);
  not not_4 (not_4_out, RE);
  and and_4 (and_4_out, not_4_out, AS);
  not not_5 (not_5_out, RE);
  and and_5 (and_5_out, not_5_out, VR);
  not not_6 (not_6_out, RE);
  and and_6 (and_6_out, not_6_out, not_7_out, SE);
  not not_7 (not_7_out, AS);
  not not_8 (not_8_out, RE);
  and and_7 (and_7_out, not_8_out, VR);
  not not_9 (not_9_out, VR);
  and and_8 (and_8_out, not_9_out, AS);
  or or_2 (f, SE, AS, VR, RE);
  not not_10 (not_10_out, RE);
  not not_11 (not_11_out, VR);
  and and_9 (and_9_out, not_10_out, not_11_out, SE);
  not not_12 (not_12_out, RE);
  and and_10 (and_10_out, not_12_out, not_13_out, AS);
  not not_13 (not_13_out, VR);
  or or_3 (a, and_1_out, and_2_out, RE);
  or or_4 (c, and_3_out, and_4_out, and_5_out);
  or or_5 (d, and_6_out, and_7_out);
  or or_6 (e, and_8_out, RE);
  or or_7 (g, and_9_out, and_10_out);
endmodule

module Caixa_Display2 (
  input  RE,
  input  VR,
  input  AS,
  input  SE,
  output a,
  output b,
  output c,
  output d,
  output e,
  output f,
  output g
);

  wire and_3_out, and_4_out, and_5_out, and_6_out, and_7_out, not_1_out, not_2_out, not_3_out, not_4_out,
       not_5_out, not_6_out, not_7_out, not_8_out;

  or or_1 (a, SE, AS, VR, RE);
  not not_1 (not_1_out, RE);
  and and_1 (b, not_1_out, VR);
  not not_2 (not_2_out, RE);
  not not_3 (not_3_out, VR);
  and and_2 (c, not_2_out, not_3_out, AS);
  not not_4 (not_4_out, VR);
  and and_3 (and_3_out, not_4_out, SE);
  not not_5 (not_5_out, VR);
  and and_4 (and_4_out, not_5_out, AS);
  not not_6 (not_6_out, AS);
  and and_5 (and_5_out, not_6_out, SE);
  or or_2 (f, SE, AS, VR, RE);
  not not_7 (not_7_out, VR);
  and and_6 (and_6_out, not_7_out, SE);
  not not_8 (not_8_out, VR);
  and and_7 (and_7_out, not_8_out, AS);
  or or_3 (d, and_3_out, and_4_out, RE);
  or or_4 (e, and_5_out, VR, RE);
  or or_5 (g, and_6_out, and_7_out, RE);
endmodule
