// Logisim project Projeto3.circ as structural Verilog: 6 circuits, main circuit main
module main (
);

  wire caixa_led_1_s, xswitch_1_p1, xswitch_2_p1, xswitch_3_p1, xswitch_4_p1;
  wire [6:0] caixa_matriza_1_out_5, caixa_matriza_1_out_6, caixa_matrizb_1_out_5, caixa_matrizb_1_out_6,
       caixa_matrizc_1_out_5, caixa_matrizc_1_out_6, caixa_matrizd_1_out_5, caixa_matrizd_1_out_6;

  // XSwitch xswitch_1: pin names not known; wires that end beside it: xswitch_1_p1
  // XSwitch xswitch_2: pin names not known; wires that end beside it: xswitch_2_p1
  // XSwitch xswitch_3: pin names not known; wires that end beside it: xswitch_3_p1
  // XSwitch xswitch_4: pin names not known; wires that end beside it: xswitch_4_p1
  Caixa_Led caixa_led_1 (.A(xswitch_1_p1), .B(xswitch_2_p1), .C(xswitch_4_p1), .D(xswitch_3_p1), .S(caixa_led_1_s));
  Caixa_MatrizA caixa_matriza_1 (
    .A(xswitch_1_p1), .B(xswitch_2_p1), .C(xswitch_4_p1), .D(xswitch_3_p1), .out_5(caixa_matriza_1_out_5),
    .out_6(caixa_matriza_1_out_6));
  Caixa_MatrizB caixa_matrizb_1 (
    .A(xswitch_1_p1), .B(xswitch_2_p1), .C(xswitch_4_p1), .D(xswitch_3_p1), .out_5(caixa_matrizb_1_out_5),
    .out_6(caixa_matrizb_1_out_6));
  Caixa_MatrizC caixa_matrizc_1 (
    .A(xswitch_1_p1), .B(xswitch_2_p1), .C(xswitch_4_p1), .D(xswitch_3_p1), .out_5(caixa_matrizc_1_out_5),
    .out_6(caixa_matrizc_1_out_6));
  Caixa_MatrizD caixa_matrizd_1 (
    .A(xswitch_1_p1), .B(xswitch_2_p1), .C(xswitch_4_p1), .D(xswitch_3_p1), .out_5(caixa_matrizd_1_out_5),
    .out_6(caixa_matrizd_1_out_6));
  LED led_1 (.in(caixa_led_1_s));
  DotMatrix dotmatrix_1 (
    .col0(caixa_matriza_1_out_5), .col1(caixa_matriza_1_out_6), .col3(caixa_matrizb_1_out_5),
    .col4(caixa_matrizb_1_out_6));  // open: col2
  DotMatrix dotmatrix_2 (
    .col0(caixa_matrizc_1_out_5), .col1(caixa_matrizc_1_out_6), .col3(caixa_matrizd_1_out_5),
    .col4(caixa_matrizd_1_out_6));  // open: col2

  // Notes on the sheet:
  //   B
  //   A
  //   D
  //   C
  //   ----Satisfatório
  //   ---Insatisfatório
  //   TA
  //   TB
  //   --------------Nivel MAX
  //   TD
  //   TC
  //   -----------Temp MIN
  //   LEGENDA:
  //   Sensores:
  //   Matrizes:
  //   LED:
  //   aceso:
  //   A - Sensor de nível do tanque A
  //   B - Sensor de nível do tanque B
  //   C - Sensor de temperatura do tanque C
  //   D - Sensor de temperatura do tanque D
  //   TA - Representação do tanque A
  //   TB - Representação do tanque B
  //   TC - Representação do tanque C
  //   TD - Representação do tanque D
  //   - nível do tanque A ou B muito alto e 
  //   - temperatura do tanque C ou D muito baixa
endmodule

module Caixa_Led (
  input  A,
  input  B,
  input  C,
  input  D,
  output S
);

  wire and_1_out, and_2_out, and_3_out, and_4_out;

  and and_1 (and_1_out, B, D);
  and and_2 (and_2_out, B, C);
  and and_3 (and_3_out, A, D);
  and and_4 (and_4_out, A, C);
  or or_1 (S, and_1_out, and_2_out, and_3_out, and_4_out);
endmodule

module Caixa_MatrizA (
  input  A,
  input  B,
  input  C,
  input  D,
  output [6:0] out_5,
  output [6:0] out_6
);


  assign out_5 = {2'b00, {2{A}}, 3'b111};
  assign out_6 = {2'b00, {2{A}}, 3'b111};
endmodule

module Caixa_MatrizB (
  input  A,
  input  B,
  input  C,
  input  D,
  output [6:0] out_5,
  output [6:0] out_6
);


  assign out_5 = {2'b00, {2{B}}, 3'b111};
  assign out_6 = {2'b00, {2{B}}, 3'b111};
endmodule

module Caixa_MatrizC (
  input  A,
  input  B,
  input  C,
  input  D,
  output [6:0] out_5,
  output [6:0] out_6
);

  not not_1 (out_5[2], C);
  not not_2 (out_5[3], C);
  not not_3 (out_5[4], C);
  not not_4 (out_5[5], C);

  assign {out_5[6], out_5[1:0]} = 3'b011;
  assign out_6 = {1'b0, out_5[5:2], 2'b11};
endmodule

module Caixa_MatrizD (
  input  A,
  input  B,
  input  C,
  input  D,
  output [6:0] out_5,
  output [6:0] out_6
);

  not not_1 (out_5[2], D);
  not not_2 (out_5[3], D);
  not not_3 (out_5[4], D);
  not not_4 (out_5[5], D);

  assign {out_5[6], out_5[1:0]} = 3'b011;
  assign out_6 = {1'b0, out_5[5:2], 2'b11};
endmodule
