// Logisim project Projeto5.circ as structural Verilog: 12 circuits, main circuit main
module main (
);

  wire caixa_carac1_1_a, caixa_carac2m1_1_a, caixa_carac2m1_1_b, caixa_carac2m1_1_c, caixa_carac2m1_1_d,
       caixa_carac2m1_1_e, caixa_carac2m1_1_f, caixa_carac2m1_1_g, caixa_carac2m2_1_a, caixa_carac2m2_1_b,
       caixa_carac2m2_1_c, caixa_carac2m2_1_d, caixa_carac2m2_1_e, caixa_carac2m2_1_f, caixa_carac2m2_1_g,
       caixa_carac2m3_1_a, caixa_carac2m3_1_b, caixa_carac2m3_1_c, caixa_carac2m3_1_d, caixa_carac2m3_1_e,
       caixa_carac2m3_1_f, caixa_carac2m3_1_g, caixa_carac2m4_1_a, caixa_carac2m4_1_b, caixa_carac2m4_1_c,
       caixa_carac2m4_1_d, caixa_carac2m4_1_e, caixa_carac2m4_1_f, caixa_carac2m4_1_g, caixa_carac3m1_1_a,
       caixa_carac3m1_1_b, caixa_carac3m1_1_c, caixa_carac3m1_1_d, caixa_carac3m1_1_e, caixa_carac3m1_1_f,
       caixa_carac3m1_1_g, caixa_carac3m2_1_a, caixa_carac3m2_1_b, caixa_carac3m2_1_c, caixa_carac3m2_1_d,
       caixa_carac3m2_1_e, caixa_carac3m2_1_f, caixa_carac3m2_1_g, caixa_carac3m3_1_a, caixa_carac3m3_1_b,
       caixa_carac3m3_1_c, caixa_carac3m3_1_d, caixa_carac3m3_1_e, caixa_carac3m3_1_f, caixa_carac3m3_1_g,
       caixa_carac3m4_1_a, caixa_carac3m4_1_b, caixa_carac3m4_1_c, caixa_carac3m4_1_d, caixa_carac3m4_1_e,
       caixa_carac3m4_1_f, caixa_carac3m4_1_g, caixa_maquinas_1_sm1, caixa_maquinas_1_sm2,
       caixa_maquinas_1_sm3, caixa_maquinas_1_sm4, caixa_nome_1_s, xswitch_1_p1, xswitch_2_p1, xswitch_3_p1,
       xswitch_4_p1;

  // XSwitch xswitch_1: pin names not known; wires that end beside it: xswitch_1_p1
  // XSwitch xswitch_2: pin names not known; wires that end beside it: xswitch_2_p1
  // XSwitch xswitch_3: pin names not known; wires that end beside it: xswitch_3_p1
  // XSwitch xswitch_4: pin names not known; wires that end beside it: xswitch_4_p1
  Caixa_Maquinas caixa_maquinas_1 (
    .M1(xswitch_1_p1), .M2(xswitch_2_p1), .M3(xswitch_4_p1), .M4(xswitch_3_p1), .SM1(caixa_maquinas_1_sm1),
    .SM2(caixa_maquinas_1_sm2), .SM3(caixa_maquinas_1_sm3), .SM4(caixa_maquinas_1_sm4));
  Caixa_nome caixa_nome_1 (
    .M1(xswitch_1_p1), .M2(xswitch_2_p1), .M3(xswitch_4_p1), .M4(xswitch_3_p1), .S(caixa_nome_1_s));
  Caixa_carac1 caixa_carac1_1 (
    .M1(xswitch_1_p1), .M2(xswitch_2_p1), .M3(xswitch_4_p1), .M4(xswitch_3_p1), .a(caixa_carac1_1_a));
  Caixa_Carac2M1 caixa_carac2m1_1 (
    .M1(xswitch_1_p1), .M2(xswitch_2_p1), .M3(xswitch_4_p1), .M4(xswitch_3_p1), .e(caixa_carac2m1_1_e),
    .d(caixa_carac2m1_1_d), .c(caixa_carac2m1_1_c), .g(caixa_carac2m1_1_g), .f(caixa_carac2m1_1_f),
    .a(caixa_carac2m1_1_a), .b(caixa_carac2m1_1_b));
  Caixa_Carac3M1 caixa_carac3m1_1 (
    .M1(xswitch_1_p1), .M2(xswitch_2_p1), .M3(xswitch_4_p1), .M4(xswitch_3_p1), .e(caixa_carac3m1_1_e),
    .d(caixa_carac3m1_1_d), .c(caixa_carac3m1_1_c), .g(caixa_carac3m1_1_g), .f(caixa_carac3m1_1_f),
    .a(caixa_carac3m1_1_a), .b(caixa_carac3m1_1_b));
  Caixa_Carac2M2 caixa_carac2m2_1 (
    .M1(xswitch_1_p1), .M2(xswitch_2_p1), .M3(xswitch_4_p1), .M4(xswitch_3_p1), .e(caixa_carac2m2_1_e),
    .d(caixa_carac2m2_1_d), .c(caixa_carac2m2_1_c), .g(caixa_carac2m2_1_g), .f(caixa_carac2m2_1_f),
    .a(caixa_carac2m2_1_a), .b(caixa_carac2m2_1_b));
  Caixa_Carac3M2 caixa_carac3m2_1 (
    .M1(xswitch_1_p1), .M2(xswitch_2_p1), .M3(xswitch_4_p1), .M4(xswitch_3_p1), .e(caixa_carac3m2_1_e),
    .d(caixa_carac3m2_1_d), .c(caixa_carac3m2_1_c), .g(caixa_carac3m2_1_g), .f(caixa_carac3m2_1_f),
    .a(caixa_carac3m2_1_a), .b(caixa_carac3m2_1_b));
  Caixa_Carac2M3 caixa_carac2m3_1 (
    .M1(xswitch_1_p1), .M2(xswitch_2_p1), .M3(xswitch_4_p1), .M4(xswitch_3_p1), .e(caixa_carac2m3_1_e),
    .d(caixa_carac2m3_1_d), .c(caixa_carac2m3_1_c), .g(caixa_carac2m3_1_g), .f(caixa_carac2m3_1_f),
    .a(caixa_carac2m3_1_a), .b(caixa_carac2m3_1_b));
  Caixa_Carac3M3 caixa_carac3m3_1 (
    .M1(xswitch_1_p1), .M2(xswitch_2_p1), .M3(xswitch_4_p1), .M4(xswitch_3_p1), .e(caixa_carac3m3_1_e),
    .d(caixa_carac3m3_1_d), .c(caixa_carac3m3_1_c), .g(caixa_carac3m3_1_g), .f(caixa_carac3m3_1_f),
    .a(caixa_carac3m3_1_a), .b(caixa_carac3m3_1_b));
  Caixa_Carac2M4 caixa_carac2m4_1 (
    .M1(xswitch_1_p1), .M2(xswitch_2_p1), .M3(xswitch_4_p1), .M4(xswitch_3_p1), .e(caixa_carac2m4_1_e),
    .d(caixa_carac2m4_1_d), .c(caixa_carac2m4_1_c), .g(caixa_carac2m4_1_g), .f(caixa_carac2m4_1_f),
    .a(caixa_carac2m4_1_a), .b(caixa_carac2m4_1_b));
  Caixa_Carac3M4 caixa_carac3m4_1 (
    .M1(xswitch_1_p1), .M2(xswitch_2_p1), .M3(xswitch_4_p1), .M4(xswitch_3_p1), .e(caixa_carac3m4_1_e),
    .d(caixa_carac3m4_1_d), .c(caixa_carac3m4_1_c), .g(caixa_carac3m4_1_g), .f(caixa_carac3m4_1_f),
    .a(caixa_carac3m4_1_a), .b(caixa_carac3m4_1_b));
  _7_Segment_Display u_7_segment_display_1 (
    .a(caixa_nome_1_s), .e(caixa_nome_1_s), .c(caixa_nome_1_s));  // open: g, f, b, d, dp
  _7_Segment_Display u_7_segment_display_2 (.b(caixa_nome_1_s), .c(caixa_nome_1_s));  // open: g, f, a, e, d, dp
  _7_Segment_Display u_7_segment_display_3 (
    .g(caixa_carac2m1_1_g), .f(caixa_carac2m1_1_f), .a(caixa_carac2m1_1_a), .b(caixa_carac2m1_1_b),
    .e(caixa_carac2m1_1_e), .d(caixa_carac2m1_1_d), .c(caixa_carac2m1_1_c));  // open: dp
  _7_Segment_Display u_7_segment_display_4 (
    .f(caixa_carac1_1_a), .a(caixa_carac1_1_a), .b(caixa_carac1_1_a), .e(caixa_carac1_1_a),
    .d(caixa_carac1_1_a), .c(caixa_carac1_1_a));  // open: g, dp
  LED led_1 (.in(caixa_maquinas_1_sm1));
  _7_Segment_Display u_7_segment_display_5 (
    .g(caixa_carac3m1_1_g), .f(caixa_carac3m1_1_f), .a(caixa_carac3m1_1_a), .b(caixa_carac3m1_1_b),
    .e(caixa_carac3m1_1_e), .d(caixa_carac3m1_1_d), .c(caixa_carac3m1_1_c));  // open: dp
  _7_Segment_Display u_7_segment_display_6 (
    .a(caixa_nome_1_s), .e(caixa_nome_1_s), .c(caixa_nome_1_s));  // open: g, f, b, d, dp
  _7_Segment_Display u_7_segment_display_7 (
    .g(caixa_nome_1_s), .a(caixa_nome_1_s), .b(caixa_nome_1_s), .e(caixa_nome_1_s), .d(caixa_nome_1_s));  // open: f, c, dp
  _7_Segment_Display u_7_segment_display_8 (
    .f(caixa_carac1_1_a), .a(caixa_carac1_1_a), .b(caixa_carac1_1_a), .e(caixa_carac1_1_a),
    .d(caixa_carac1_1_a), .c(caixa_carac1_1_a));  // open: g, dp
  _7_Segment_Display u_7_segment_display_9 (
    .g(caixa_carac2m2_1_g), .f(caixa_carac2m2_1_f), .a(caixa_carac2m2_1_a), .b(caixa_carac2m2_1_b),
    .e(caixa_carac2m2_1_e), .d(caixa_carac2m2_1_d), .c(caixa_carac2m2_1_c));  // open: dp
  LED led_2 (.in(caixa_maquinas_1_sm2));
  _7_Segment_Display u_7_segment_display_10 (
    .g(caixa_carac3m2_1_g), .f(caixa_carac3m2_1_f), .a(caixa_carac3m2_1_a), .b(caixa_carac3m2_1_b),
    .e(caixa_carac3m2_1_e), .d(caixa_carac3m2_1_d), .c(caixa_carac3m2_1_c));  // open: dp
  _7_Segment_Display u_7_segment_display_11 (
    .a(caixa_nome_1_s), .e(caixa_nome_1_s), .c(caixa_nome_1_s));  // open: g, f, b, d, dp
  _7_Segment_Display u_7_segment_display_12 (
    .g(caixa_nome_1_s), .a(caixa_nome_1_s), .b(caixa_nome_1_s), .d(caixa_nome_1_s), .c(caixa_nome_1_s));  // open: f, e, dp
  _7_Segment_Display u_7_segment_display_13 (
    .f(caixa_carac1_1_a), .a(caixa_carac1_1_a), .b(caixa_carac1_1_a), .e(caixa_carac1_1_a),
    .d(caixa_carac1_1_a), .c(caixa_carac1_1_a));  // open: g, dp
  _7_Segment_Display u_7_segment_display_14 (
    .g(caixa_carac2m3_1_g), .f(caixa_carac2m3_1_f), .a(caixa_carac2m3_1_a), .b(caixa_carac2m3_1_b),
    .e(caixa_carac2m3_1_e), .d(caixa_carac2m3_1_d), .c(caixa_carac2m3_1_c));  // open: dp
  LED led_3 (.in(caixa_maquinas_1_sm3));
  _7_Segment_Display u_7_segment_display_15 (
    .g(caixa_carac3m3_1_g), .f(caixa_carac3m3_1_f), .a(caixa_carac3m3_1_a), .b(caixa_carac3m3_1_b),
    .e(caixa_carac3m3_1_e), .d(caixa_carac3m3_1_d), .c(caixa_carac3m3_1_c));  // open: dp
  _7_Segment_Display u_7_segment_display_16 (
    .a(caixa_nome_1_s), .e(caixa_nome_1_s), .c(caixa_nome_1_s));  // open: g, f, b, d, dp
  _7_Segment_Display u_7_segment_display_17 (
    .g(caixa_nome_1_s), .f(caixa_nome_1_s), .b(caixa_nome_1_s), .c(caixa_nome_1_s));  // open: a, e, d, dp
  _7_Segment_Display u_7_segment_display_18 (
    .f(caixa_carac1_1_a), .a(caixa_carac1_1_a), .b(caixa_carac1_1_a), .e(caixa_carac1_1_a),
    .d(caixa_carac1_1_a), .c(caixa_carac1_1_a));  // open: g, dp
  _7_Segment_Display u_7_segment_display_19 (
    .g(caixa_carac2m4_1_g), .f(caixa_carac2m4_1_f), .a(caixa_carac2m4_1_a), .b(caixa_carac2m4_1_b),
    .e(caixa_carac2m4_1_e), .d(caixa_carac2m4_1_d), .c(caixa_carac2m4_1_c));  // open: dp
  LED led_4 (.in(caixa_maquinas_1_sm4));
  _7_Segment_Display u_7_segment_display_20 (
    .g(caixa_carac3m4_1_g), .f(caixa_carac3m4_1_f), .a(caixa_carac3m4_1_a), .b(caixa_carac3m4_1_b),
    .e(caixa_carac3m4_1_e), .d(caixa_carac3m4_1_d), .c(caixa_carac3m4_1_c));  // open: dp

  // Notes on the sheet:
  //   M1
  //   M2
  //   M4
  //   M3
  //   ---Ligado
  //   ---Desligado
  //   Entradas e Display:
  //   M1 - Maquina 1
  //   M2 - Maquina 2
  //   M3 - Maquina 3
  //   M4 - Maquina 4
  //   LEGENDA:
  //   Displays inferiores:
  //   ON - Maquina ligada
  //   OFF - Maquina desligada
endmodule

module Caixa_Maquinas (
  input  M1,
  input  M2,
  input  M3,
  input  M4,
  output SM1,
  output SM2,
  output SM3,
  output SM4
);

  wire and_1_out, and_2_out, and_3_out, and_4_out, and_5_out, not_1_out, not_2_out, not_3_out, not_4_out,
       not_5_out, not_6_out, not_7_out, not_8_out;

  not not_1 (not_1_out, M1);
  and and_1 (and_1_out, not_1_out, M3);
  not not_2 (not_2_out, M2);
  and and_2 (and_2_out, not_2_out, M3);
  not not_3 (not_3_out, M1);
  not not_4 (not_4_out, M2);
  and and_3 (and_3_out, not_3_out, not_4_out, M4);
  not not_5 (not_5_out, M1);
  and and_4 (and_4_out, not_5_out, not_6_out, M4);
  not not_6 (not_6_out, M3);
  not not_7 (not_7_out, M2);
  not not_8 (not_8_out, M3);
  and and_5 (and_5_out, not_7_out, not_8_out, M4);
  or or_1 (SM3, and_1_out, and_2_out);
  or or_2 (SM4, and_3_out, and_4_out, and_5_out);

  assign SM1 = M1;
  assign SM2 = M2;
endmodule

module Caixa_nome (
  input  M1,
  input  M2,
  input  M3,
  input  M4,
  output S
);


  assign S = 1'b1;
endmodule

module Caixa_carac1 (
  input  M1,
  input  M2,
  input  M3,
  input  M4,
  output a
);


  assign a = 1'b1;
endmodule

module Caixa_Carac2M1 (
  input  M1,
  input  M2,
  input  M3,
  input  M4,
  output e,
  output d,
  output c,
  output g,
  output f,
  output a,
  output b
);

  not not_1 (g, M1);

  assign a = 1'b1;
  assign b = M1;
  assign c = M1;
  assign d = 1'b0;
  assign e = 1'b1;
  assign f = 1'b1;
endmodule

module Caixa_Carac3M1 (
  input  M1,
  input  M2,
  input  M3,
  input  M4,
  output e,
  output d,
  output c,
  output g,
  output f,
  output a,
  output b
);

  not not_1 (e, M1);
  not not_2 (g, M1);
  not not_3 (f, M1);
  not not_4 (a, M1);

  assign b = 1'b0;
  assign c = 1'b0;
  assign d = 1'b0;
endmodule

module Caixa_Carac2M2 (
  input  M1,
  input  M2,
  input  M3,
  input  M4,
  output e,
  output d,
  output c,
  output g,
  output f,
  output a,
  output b
);

  not not_1 (g, M2);

  assign a = 1'b1;
  assign b = M2;
  assign c = M2;
  assign d = 1'b0;
  assign e = 1'b1;
  assign f = 1'b1;
endmodule

module Caixa_Carac3M2 (
  input  M1,
  input  M2,
  input  M3,
  input  M4,
  output e,
  output d,
  output c,
  output g,
  output f,
  output a,
  output b
);

  not not_1 (e, M2);
  not not_2 (g, M2);
  not not_3 (f, M2);
  not not_4 (a, M2);

  assign b = 1'b0;
  assign c = 1'b0;
  assign d = 1'b0;
endmodule

module Caixa_Carac2M3 (
  input  M1,
  input  M2,
  input  M3,
  input  M4,
  output e,
  output d,
  output c,
  output g,
  output f,
  output a,
  output b
);

  wire and_1_out, and_2_out, and_3_out, and_4_out, and_5_out, not_1_out, not_2_out, not_3_out, not_4_out,
       not_5_out;

  not not_1 (not_1_out, M1);
  and and_1 (and_1_out, not_1_out, M3);
  not not_2 (not_2_out, M2);
  and and_2 (and_2_out, not_2_out, M3);
  not not_3 (not_3_out, M3);
  and and_3 (and_3_out, M1, M2);
  not not_4 (not_4_out, M1);
  and and_4 (and_4_out, not_4_out, M3);
  not not_5 (not_5_out, M2);
  and and_5 (and_5_out, not_5_out, M3);
  or or_1 (c, and_1_out, and_2_out);
  or or_2 (g, not_3_out, and_3_out);
  or or_3 (b, and_4_out, and_5_out);

  assign a = 1'b1;
  assign d = 1'b0;
  assign e = 1'b1;
  assign f = 1'b1;
endmodule

module Caixa_Carac3M3 (
  input  M1,
  input  M2,
  input  M3,
  input  M4,
  output e,
  output d,
  output c,
  output g,
  output f,
  output a,
  output b
);

  wire and_1_out, and_2_out, and_3_out, and_4_out, not_1_out, not_2_out, not_3_out, not_4_out;

  not not_1 (not_1_out, M3);
  and and_1 (and_1_out, M1, M2);
  not not_2 (not_2_out, M3);
  and and_2 (and_2_out, M1, M2);
  not not_3 (not_3_out, M3);
  and and_3 (and_3_out, M1, M2);
  not not_4 (not_4_out, M3);
  and and_4 (and_4_out, M1, M2);
  or or_1 (e, not_1_out, and_1_out);
  or or_2 (g, not_2_out, and_2_out);
  or or_3 (f, not_3_out, and_3_out);
  or or_4 (a, not_4_out, and_4_out);

  assign b = 1'b0;
  assign c = 1'b0;
  assign d = 1'b0;
endmodule

module Caixa_Carac2M4 (
  input  M1,
  input  M2,
  input  M3,
  input  M4,
  output e,
  output d,
  output c,
  output g,
  output f,
  output a,
  output b
);

  wire and_1_out, and_2_out, and_3_out, and_4_out, and_5_out, and_6_out, and_7_out, and_8_out, and_9_out,
       not_1_out, not_2_out, not_3_out, not_4_out, not_5_out, not_6_out, not_7_out, not_8_out, not_9_out,
       not_10_out, not_11_out, not_12_out, not_13_out;

  not not_1 (not_1_out, M1);
  not not_2 (not_2_out, M2);
  and and_1 (and_1_out, not_1_out, not_2_out, M4);
  not not_3 (not_3_out, M1);
  and and_2 (and_2_out, not_3_out, not_4_out, M4);
  not not_4 (not_4_out, M3);
  not not_5 (not_5_out, M2);
  and and_3 (and_3_out, not_5_out, not_6_out, M4);
  not not_6 (not_6_out, M3);
  not not_7 (not_7_out, M4);
  and and_4 (and_4_out, M2, M3);
  and and_5 (and_5_out, M1, M3);
  and and_6 (and_6_out, M1, M2);
  not not_8 (not_8_out, M1);
  not not_9 (not_9_out, M2);
  and and_7 (and_7_out, not_8_out, not_9_out, M4);
  not not_10 (not_10_out, M1);
  not not_11 (not_11_out, M3);
  and and_8 (and_8_out, not_10_out, not_11_out, M4);
  not not_12 (not_12_out, M2);
  and and_9 (and_9_out, not_12_out, not_13_out, M4);
  not not_13 (not_13_out, M3);
  or or_1 (c, and_1_out, and_2_out, and_3_out);
  or or_2 (g, not_7_out, and_4_out, and_5_out, and_6_out);
  or or_3 (b, and_7_out, and_8_out, and_9_out);

  assign a = 1'b1;
  assign d = 1'b0;
  assign e = 1'b1;
  assign f = 1'b1;
endmodule

module Caixa_Carac3M4 (
  input  M1,
  input  M2,
  input  M3,
  input  M4,
  output e,
  output d,
  output c,
  output g,
  output f,
  output a,
  output b
);

  wire and_1_out, and_2_out, and_3_out, and_4_out, and_5_out, and_6_out, and_7_out, and_8_out, and_9_out,
       and_10_out, and_11_out, and_12_out, not_1_out, not_2_out, not_3_out, not_4_out;

  not not_1 (not_1_out, M4);
  and and_1 (and_1_out, M2, M3);
  and and_2 (and_2_out, M1, M3);
  and and_3 (and_3_out, M1, M2);
  not not_2 (not_2_out, M4);
  and and_4 (and_4_out, M2, M3);
  and and_5 (and_5_out, M1, M3);
  and and_6 (and_6_out, M1, M2);
  not not_3 (not_3_out, M4);
  and and_7 (and_7_out, M2, M3);
  and and_8 (and_8_out, M1, M3);
  and and_9 (and_9_out, M1, M2);
  not not_4 (not_4_out, M4);
  and and_10 (and_10_out, M2, M3);
  and and_11 (and_11_out, M1, M3);
  and and_12 (and_12_out, M1, M2);
  or or_1 (e, not_1_out, and_1_out, and_2_out, and_3_out);
  or or_2 (g, not_2_out, and_4_out, and_5_out, and_6_out);
  or or_3 (f, not_3_out, and_7_out, and_8_out, and_9_out);
  or or_4 (a, not_4_out, and_10_out, and_11_out, and_12_out);

  assign b = 1'b0;
  assign c = 1'b0;
  assign d = 1'b0;
endmodule
