// Logisim project datapath.circ as structural Verilog: 3 circuits, main circuit Datapath
module Datapath (
  input  Clear,
  input  Reset,
  input  Clear_2
);

  wire ALU_p4, and_1_out, BRANCH, Clock_out, Decodificador_p2, Decodificador_p6, Decodificador_p7,
       ESCREVEMEM, ESCREVEREG, JUMP, LEMEM, MEMPARAREG, mips_ram_1_p4, not_1_out, ORIGALU, REGDST,
       registerfile_1_p7, wordaddress_1_p2, wordaddress_2_p2;
  wire [1:0] OPALU;
  wire [3:0] alucontrol_1_operation;
  wire [4:0] Decodificador_p3, Decodificador_p4, multiplexer_2_out;
  wire [5:0] Decodificador_p1, Decodificador_p5;
  wire [31:0] adder_1_out, ALU_p5, Branch_p3, \Extensão_p2 , JumpAddress_p1, JumpAddress_p2, mips_ram_2_p4,
       multiplexer_1_out, multiplexer_3_out, register_1_q, registerfile_1_p1, registerfile_1_p8;

  Clock Clock (.out(Clock_out));
  Register #(.width(32)) register_1 (
    .D(multiplexer_1_out), .Q(register_1_q), .clk(Clock_out), .clr(Reset));  // open: en
  // WordAddress wordaddress_1: pin names not known; wires that end beside it: register_1_q, wordaddress_1_p2, wordaddress_1_p2, 1'b0, 4'b1111
  Adder #(.width(32)) adder_1 (.a(32'h4), .b(register_1_q), .out(adder_1_out));  // open: cin, cout
  // MIPS_RAM mips_ram_1: pin names not known; wires that end beside it: 1'b0, 1'b1, Clear, mips_ram_1_p4, mips_ram_1_p4
  // InstructionDecode Decodificador: pin names not known; wires that end beside it: Decodificador_p1, Decodificador_p2, Decodificador_p3, Decodificador_p4, Decodificador_p5, Decodificador_p6, Decodificador_p7
  Control Controle (
    .op(Decodificador_p1), .Jump(JUMP), .RegDst(REGDST), .Branch(BRANCH), .LeMem(LEMEM),
    .MemparaReg(MEMPARAREG), .OpALU(OPALU), .EscreveMem(ESCREVEMEM), .OrigALU(ORIGALU),
    .EscreveReg(ESCREVEREG));
  not not_1 (not_1_out, Clock_out);
  Multiplexer #(.width(32), .enable("false")) multiplexer_1 (
    .in0(JumpAddress_p2), .in1(JumpAddress_p1), .out(multiplexer_1_out), .sel(JUMP));
  // JumpAddress JumpAddress: pin names not known; wires that end beside it: JumpAddress_p1, JumpAddress_p2, Decodificador_p7
  Multiplexer #(.width(5), .enable("false")) multiplexer_2 (
    .in0(Decodificador_p3), .in1(Decodificador_p4), .out(multiplexer_2_out), .sel(REGDST));
  ALUcontrol alucontrol_1 (.funct(Decodificador_p5), .OpALU(OPALU), .Operation(alucontrol_1_operation));
  // SignExtend Extensão: pin names not known; wires that end beside it: Decodificador_p6, \Extensão_p2 
  // RegisterFile registerfile_1: pin names not known; wires that end beside it: registerfile_1_p1, not_1_out, ESCREVEREG, multiplexer_2_out, Decodificador_p2, Decodificador_p3, registerfile_1_p7, registerfile_1_p8
  Multiplexer #(.width(32), .enable("false")) multiplexer_3 (
    .in0(registerfile_1_p8), .in1(\Extensão_p2 ), .out(multiplexer_3_out), .sel(ORIGALU));
  // ALU ALU: pin names not known; wires that end beside it: registerfile_1_p7, multiplexer_3_out, alucontrol_1_operation, ALU_p4, ALU_p5
  // BranchAddress Branch: pin names not known; wires that end beside it: adder_1_out, \Extensão_p2 , Branch_p3
  // WordAddress wordaddress_2: pin names not known; wires that end beside it: ALU_p5, wordaddress_2_p2, wordaddress_2_p2, registerfile_1_p8, ESCREVEMEM, 4'b1111
  Multiplexer #(.width(32), .enable("false")) multiplexer_4 (
    .in0(adder_1_out), .in1(Branch_p3), .out(JumpAddress_p2), .sel(and_1_out));
  and and_1 (and_1_out, BRANCH, ALU_p4);
  // MIPS_RAM mips_ram_2: pin names not known; wires that end beside it: Clock_out, LEMEM, Clear_2, mips_ram_2_p4
  Multiplexer #(.width(32), .enable("false")) multiplexer_5 (
    .in0(ALU_p5), .in1(mips_ram_2_p4), .out(registerfile_1_p1), .sel(MEMPARAREG));

  // Notes on the sheet:
  //   PC
  //   Memória de Instruções
  //   Memória de Dados
endmodule

module Control (
  input  [5:0] op,
  output Jump,
  output RegDst,
  output Branch,
  output LeMem,
  output MemparaReg,
  output [1:0] OpALU,
  output EscreveMem,
  output OrigALU,
  output EscreveReg
);

  wire and_2_out;

  and and_1 (OpALU[1], ~op[5], ~op[4], ~op[3], ~op[2], ~op[1], ~op[0]);  // AND_Gate
  and and_2 (and_2_out, ~op[5], ~op[4], op[3], ~op[2], ~op[1], ~op[0]);  // AND_Gate
  and and_3 (LeMem, op[5], ~op[4], ~op[3], ~op[2], op[1], op[0]);  // AND_Gate
  and and_4 (EscreveMem, op[5], ~op[4], op[3], ~op[2], op[1], op[0]);  // AND_Gate
  and and_5 (Branch, ~op[5], ~op[4], ~op[3], op[2], ~op[1], ~op[0]);  // AND_Gate
  and and_6 (Jump, ~op[5], ~op[4], ~op[3], ~op[2], op[1], ~op[0]);  // AND_Gate
  or or_1 (OrigALU, LeMem, and_2_out, EscreveMem);
  or or_2 (EscreveReg, OpALU[1], and_2_out, LeMem);

  assign MemparaReg = LeMem;
  assign OpALU[0] = Branch;
  assign RegDst = OpALU[1];

  // Notes on the sheet:
  //   Tipo R
  //   addi
  //   lw
  //   sw
  //   beq
  //   jump
endmodule

module ALUcontrol (
  input  [5:0] funct,
  input  [1:0] OpALU,
  output [3:0] Operation
);

  wire and_1_out, and_2_out, and_3_out, not_1_out, not_2_out;

  and and_1 (and_1_out, funct[1], OpALU[1]);
  not not_1 (not_1_out, funct[2]);
  not not_2 (not_2_out, OpALU[1]);
  and and_2 (and_2_out, funct[0], OpALU[1]);
  and and_3 (and_3_out, funct[3], OpALU[1]);
  or or_1 (Operation[2], OpALU[0], and_1_out);
  or or_2 (Operation[1], not_1_out, not_2_out);
  or or_3 (Operation[0], and_2_out, and_3_out);

  assign Operation[3] = 1'b0;
endmodule
